# Fritzing sketch Arduino-Shield (saved by Fritzing 0.9.3b)
breadboards: 1

parts:
  U1 = Arduino Uno (Rev3)
  J2 = Screw terminal - 2 pins [package=THT]
  U2 = Max Power IR LED Kit
  R1 = Photocell (LDR) [package=THT]

nets:
  N1: U1.A0, R1.pin_0
  N2: U1.D9_PWM, U2.CONTROL
  N3: U1.D12/MISO, J2.pin2
  GND: U1.GND
  N4: J2.pin1, U2.GND, R1.pin_1
